// Logisim project CU.circ as structural Verilog
module OP_ROM (
  input  [7:0] IRin,
  input  ACTV,
  output ADD,
  output SUB,
  output MULT,
  output LD,
  output SAV,
  output BEQ,
  output BNQ,
  output PRT,
  output INP,
  output STOP,
  output FLSH
);

  wire and_1_out, and_3_out, and_5_out, and_7_out, and_9_out, and_11_out, and_13_out, and_15_out, and_17_out,
       and_19_out, and_21_out, not_1_out, not_2_out, not_3_out, not_4_out, not_5_out, not_6_out, not_7_out,
       not_8_out, not_9_out, not_10_out, not_11_out, not_12_out, not_13_out, not_14_out, not_15_out,
       not_16_out, not_17_out, not_18_out, not_19_out, not_20_out, not_21_out, not_22_out, not_23_out,
       not_24_out, not_25_out, not_26_out, not_27_out, not_28_out, not_29_out, not_30_out, not_31_out,
       or_1_out;

  not not_1 (not_1_out, IRin[3]);
  not not_2 (not_2_out, IRin[4]);
  not not_3 (not_3_out, IRin[5]);
  not not_4 (not_4_out, IRin[4]);
  not not_5 (not_5_out, IRin[5]);
  not not_6 (not_6_out, IRin[5]);
  not not_7 (not_7_out, IRin[6]);
  not not_8 (not_8_out, IRin[6]);
  or or_1 (or_1_out, IRin[4], IRin[5]);
  not not_9 (not_9_out, IRin[6]);
  not not_10 (not_10_out, IRin[7]);
  not not_11 (not_11_out, IRin[7]);
  not not_12 (not_12_out, IRin[2]);
  not not_13 (not_13_out, IRin[3]);
  not not_14 (not_14_out, IRin[5]);
  not not_15 (not_15_out, IRin[3]);
  not not_16 (not_16_out, IRin[5]);
  not not_17 (not_17_out, IRin[1]);
  not not_18 (not_18_out, IRin[2]);
  not not_19 (not_19_out, IRin[3]);
  not not_20 (not_20_out, IRin[4]);
  not not_21 (not_21_out, IRin[5]);
  not not_22 (not_22_out, IRin[6]);
  not not_23 (not_23_out, IRin[7]);
  not not_24 (not_24_out, IRin[0]);
  not not_25 (not_25_out, IRin[1]);
  not not_26 (not_26_out, IRin[2]);
  not not_27 (not_27_out, IRin[3]);
  not not_28 (not_28_out, IRin[4]);
  not not_29 (not_29_out, IRin[5]);
  not not_30 (not_30_out, IRin[6]);
  not not_31 (not_31_out, IRin[7]);
  and and_1 (and_1_out, not_1_out, not_2_out, not_3_out, IRin[6], IRin[7]);
  and and_2 (ADD, and_1_out, ACTV);
  and and_3 (and_3_out, IRin[3], not_4_out, not_5_out, IRin[6], IRin[7]);
  and and_4 (SUB, and_3_out, ACTV);
  and and_5 (and_5_out, IRin[5], IRin[6], IRin[7]);
  and and_6 (MULT, and_5_out, ACTV);
  and and_7 (and_7_out, not_6_out, not_7_out, IRin[7]);
  and and_8 (LD, and_7_out, ACTV);
  and and_9 (and_9_out, IRin[5], not_8_out, IRin[7]);
  and and_10 (SAV, and_9_out, ACTV);
  and and_11 (and_11_out, or_1_out, not_9_out, not_10_out);
  and and_12 (BEQ, and_11_out, ACTV);
  and and_13 (and_13_out, IRin[6], not_11_out);
  and and_14 (BNQ, and_13_out, ACTV);
  and and_15 (and_15_out, not_12_out, not_13_out, IRin[4], not_14_out, IRin[6], IRin[7]);
  and and_16 (PRT, and_15_out, ACTV);
  and and_17 (and_17_out, IRin[2], not_15_out, IRin[4], not_16_out, IRin[6], IRin[7]);
  and and_18 (INP, and_17_out, ACTV);
  and and_19 (and_19_out, IRin[0], not_17_out, not_18_out, not_19_out, not_20_out, not_21_out, not_22_out, not_23_out);
  and and_20 (STOP, and_19_out, ACTV);
  and and_21 (and_21_out, not_24_out, not_25_out, not_26_out, not_27_out, not_28_out, not_29_out, not_30_out, not_31_out);
  and and_22 (FLSH, and_21_out, ACTV);
endmodule

module CU (
  input  [7:0] IRin,
  input  in_2,
  output Reg0,
  output Reg1,
  output R_W,
  output ALU_L,
  output ALU_R,
  output ALU_O,
  output ALU_EXE,
  output ALU_FLAG,
  output STAT,
  output MAR_IN,
  output MAR_OUT,
  output MBR_IN,
  output MBR_OUT,
  output IR,
  output PC_INC,
  output PC_ADDR,
  output PC_OUT,
  output INP,
  output PRT
);

  wire add_sub_1_done, bnq_beq_1_done, buffer_1_out, op_rom_1_add, op_rom_1_beq, op_rom_1_bnq, op_rom_1_sub,
       or_1_out, or_2_out, or_3_out, t_ff_1_q, t_ff_1_qn;

  OP_ROM op_rom_1 (
    .IRin(IRin), .BEQ(op_rom_1_beq), .BNQ(op_rom_1_bnq), .SUB(op_rom_1_sub), .ADD(op_rom_1_add),
    .ACTV(t_ff_1_q));  // open: SAV, STOP, MULT, INP, PRT, LD, FLSH
  or or_1 (or_1_out, op_rom_1_add, op_rom_1_sub);
  Clock clock_1 ();  // open: out
  ADD_SUB add_sub_1 (
    .IRin(IRin), .Actv(or_1_out), .DONE(add_sub_1_done));  // open: ALU_EXE, ALU_L, R0, R1, ALU_R, ALU_O, R_W
  buf buffer_1 (buffer_1_out, add_sub_1_done);
  or or_2 (or_2_out, op_rom_1_beq, op_rom_1_bnq);
  BNQ_BEQ bnq_beq_1 (
    .Actv(or_2_out), .DONE(bnq_beq_1_done), .IRin(IRin));  // open: R0, PC_ADDR, R1, ALUE_EXE, STAT, ALU_L, ALU_R
  T_Flip_Flop t_ff_1 (.T(1'b1), .clk(or_3_out), .Q(t_ff_1_q), .Qn(t_ff_1_qn));  // open: reset, preset
  or or_3 (or_3_out, in_2, buffer_1_out);
  buf buffer_2 (buffer_1_out, bnq_beq_1_done);
  FETCH fetch_1 (.ACTV(t_ff_1_qn));  // open: MBR_OUT, MAR_OUT, DR, AR, MAR_IN, PC_OUT, MBR_IN, IR, PC_INC, DONE, RAM_R

  // Notes on the sheet:
  //   Control Gates
endmodule

module ADD_SUB (
  input  [7:0] IRin,
  input  Actv,
  output R0,
  output R1,
  output ALU_L,
  output ALU_R,
  output ALU_EXE,
  output ALU_O,
  output R_W,
  output DONE
);

  wire and_1_out, and_2_out, clock_1_out, not_1_out, not_2_out, not_3_out, not_4_out, not_5_out, not_6_out,
       not_7_out, or_1_out, or_2_out, or_3_out, or_4_out, RESET_out, t_ff_1_q, t_ff_1_qn, t_ff_2_q,
       t_ff_2_qn, t_ff_3_q;

  T_Flip_Flop t_ff_1 (
    .T(or_1_out), .clk(clock_1_out), .Q(t_ff_1_q), .Qn(t_ff_1_qn), .reset(RESET_out));  // open: preset
  or or_1 (or_1_out, Actv, ALU_O);
  Clock clock_1 (.out(clock_1_out));
  T_Flip_Flop t_ff_2 (.T(or_1_out), .clk(t_ff_1_qn), .Q(t_ff_2_q), .Qn(t_ff_2_qn), .reset(RESET_out));  // open: preset
  T_Flip_Flop t_ff_3 (.T(or_1_out), .clk(t_ff_2_qn), .Q(t_ff_3_q), .reset(RESET_out));  // open: Qn, preset
  not not_1 (not_1_out, t_ff_2_q);
  and LOAD1 (ALU_L, t_ff_1_q, not_1_out, not_2_out);
  not not_2 (not_2_out, t_ff_3_q);
  not not_3 (not_3_out, t_ff_1_q);
  and LOAD2 (ALU_R, not_3_out, t_ff_2_q, not_4_out);
  not not_4 (not_4_out, t_ff_3_q);
  and EXE (ALU_EXE, t_ff_1_q, t_ff_2_q, not_5_out);
  not not_5 (not_5_out, t_ff_3_q);
  not not_6 (not_6_out, t_ff_1_q);
  not not_7 (not_7_out, t_ff_2_q);
  and SAVE (ALU_O, not_6_out, not_7_out, t_ff_3_q);
  // NOT_Gate not_8 has open pins: in=t_ff_2_q, out=open
  and RESET (RESET_out, t_ff_1_q, t_ff_3_q);
  or or_2 (or_2_out, ALU_O, ALU_L);
  and and_1 (and_1_out, IRin[1], ALU_R);
  and and_2 (and_2_out, IRin[2], or_2_out);
  or or_3 (or_3_out, and_2_out, and_1_out);
  Demultiplexer #(.enable("false")) demultiplexer_1 (.out0(R0), .out1(R1), .in(or_4_out), .sel(or_3_out));
  or or_4 (or_4_out, or_2_out, ALU_R);

  assign DONE = ALU_O;
  assign R_W = ALU_O;
endmodule

module BNQ_BEQ (
  input  [7:0] IRin,
  input  Actv,
  output R0,
  output R1,
  output ALU_L,
  output ALU_R,
  output ALUE_EXE,
  output STAT,
  output PC_ADDR,
  output DONE
);

  wire and_1_out, and_2_out, clock_1_out, not_1_out, not_2_out, not_3_out, not_4_out, not_5_out, not_6_out,
       not_7_out, not_8_out, or_1_out, or_2_out, or_3_out, or_4_out, RESET_out, t_ff_1_q, t_ff_1_qn,
       t_ff_2_q, t_ff_2_qn, t_ff_3_q;

  T_Flip_Flop t_ff_1 (
    .T(or_1_out), .clk(clock_1_out), .Q(t_ff_1_q), .Qn(t_ff_1_qn), .reset(RESET_out));  // open: preset
  or or_1 (or_1_out, Actv, DONE);
  Clock clock_1 (.out(clock_1_out));
  T_Flip_Flop t_ff_2 (.T(or_1_out), .clk(t_ff_1_qn), .Q(t_ff_2_q), .Qn(t_ff_2_qn), .reset(RESET_out));  // open: preset
  T_Flip_Flop t_ff_3 (.T(or_1_out), .clk(t_ff_2_qn), .Q(t_ff_3_q), .reset(RESET_out));  // open: Qn, preset
  and LOAD1 (ALU_L, t_ff_1_q, not_1_out, not_2_out);
  not not_1 (not_1_out, t_ff_2_q);
  not not_2 (not_2_out, t_ff_3_q);
  not not_3 (not_3_out, t_ff_1_q);
  and LOAD2 (ALU_R, not_3_out, t_ff_2_q, not_4_out);
  not not_4 (not_4_out, t_ff_3_q);
  and EXE1 (ALUE_EXE, t_ff_1_q, t_ff_2_q, not_5_out);
  not not_5 (not_5_out, t_ff_3_q);
  not not_6 (not_6_out, t_ff_1_q);
  and EXE2 (DONE, not_6_out, not_7_out, t_ff_3_q);
  not not_7 (not_7_out, t_ff_2_q);
  not not_8 (not_8_out, t_ff_2_q);
  and RESET (RESET_out, t_ff_1_q, not_8_out, t_ff_3_q);
  or or_2 (or_2_out, DONE, ALU_L);
  and and_1 (and_1_out, IRin[4], ALU_R);
  and and_2 (and_2_out, IRin[5], or_2_out);
  or or_3 (or_3_out, and_2_out, and_1_out);
  or or_4 (or_4_out, or_2_out, ALU_R);
  Demultiplexer #(.enable("false")) demultiplexer_1 (.out0(R0), .out1(R1), .in(or_4_out), .sel(or_3_out));

  assign PC_ADDR = DONE;
  assign STAT = DONE;
endmodule

module FETCH (
  input  ACTV,
  output MAR_IN,
  output PC_OUT,
  output MAR_OUT,
  output AR,
  output RAM_R,
  output MBR_IN,
  output DR,
  output MBR_OUT,
  output IR,
  output PC_INC,
  output DONE
);

  wire and_7_out, clock_1_out, not_1_out, not_2_out, not_3_out, not_4_out, not_5_out, not_6_out, not_7_out,
       not_9_out, or_1_out, t_ff_1_q, t_ff_1_qn, t_ff_2_q, t_ff_2_qn, t_ff_3_q;

  T_Flip_Flop t_ff_1 (
    .T(or_1_out), .clk(clock_1_out), .Q(t_ff_1_q), .Qn(t_ff_1_qn), .reset(and_7_out));  // open: preset
  or or_1 (or_1_out, ACTV, DONE);
  Clock clock_1 (.out(clock_1_out));
  T_Flip_Flop t_ff_2 (.T(or_1_out), .clk(t_ff_1_qn), .Q(t_ff_2_q), .Qn(t_ff_2_qn), .reset(and_7_out));  // open: preset
  T_Flip_Flop t_ff_3 (.T(or_1_out), .clk(t_ff_2_qn), .Q(t_ff_3_q), .reset(and_7_out));  // open: Qn, preset
  not not_1 (not_1_out, t_ff_2_q);
  and and_1 (MAR_IN, t_ff_1_q, not_1_out, not_2_out);
  not not_2 (not_2_out, t_ff_3_q);
  not not_3 (not_3_out, t_ff_1_q);
  and and_2 (AR, not_3_out, t_ff_2_q, not_4_out);
  not not_4 (not_4_out, t_ff_3_q);
  and and_3 (RAM_R, t_ff_1_q, t_ff_2_q, not_5_out);
  not not_5 (not_5_out, t_ff_3_q);
  not not_6 (not_6_out, t_ff_1_q);
  and and_4 (DR, not_6_out, not_7_out, t_ff_3_q);
  not not_7 (not_7_out, t_ff_2_q);
  and and_5 (IR, t_ff_1_q, t_ff_3_q);
  // NOT_Gate not_8 has open pins: in=t_ff_2_q, out=open
  not not_9 (not_9_out, t_ff_1_q);
  and and_6 (DONE, not_9_out, t_ff_2_q, t_ff_3_q);
  and and_7 (and_7_out, t_ff_1_q, t_ff_2_q, t_ff_3_q);

  assign MAR_OUT = AR;
  assign MBR_IN = DR;
  assign MBR_OUT = IR;
  assign PC_INC = DONE;
  assign PC_OUT = MAR_IN;
endmodule

module SAV (
  input  [7:0] IR_IN,
  input  ACTV,
  output [3:0] RAM_A,
  output MAR_IN,
  output AR_IN,
  output MAR_OUT,
  output MBR_IN,
  output R0_OUT,
  output R1_OUT,
  output RAM_W,
  output DONE
);

  wire and_5_out, clock_1_out, not_1_out, not_2_out, not_3_out, not_4_out, not_5_out, not_6_out, not_7_out,
       not_8_out, or_1_out, t_ff_1_q, t_ff_1_qn, t_ff_2_q, t_ff_2_qn, t_ff_3_q;

  T_Flip_Flop t_ff_1 (
    .T(or_1_out), .clk(clock_1_out), .Q(t_ff_1_q), .Qn(t_ff_1_qn), .reset(and_5_out));  // open: preset
  or or_1 (or_1_out, ACTV, DONE);
  Clock clock_1 (.out(clock_1_out));
  T_Flip_Flop t_ff_2 (.T(or_1_out), .clk(t_ff_1_qn), .Q(t_ff_2_q), .Qn(t_ff_2_qn), .reset(and_5_out));  // open: preset
  T_Flip_Flop t_ff_3 (.T(or_1_out), .clk(t_ff_2_qn), .Q(t_ff_3_q), .reset(and_5_out));  // open: Qn, preset
  not not_1 (not_1_out, t_ff_2_q);
  and and_1 (MAR_IN, t_ff_1_q, not_1_out, not_2_out);
  not not_2 (not_2_out, t_ff_3_q);
  not not_3 (not_3_out, t_ff_1_q);
  and and_2 (AR_IN, not_3_out, t_ff_2_q, not_4_out);
  not not_4 (not_4_out, t_ff_3_q);
  and and_3 (MBR_IN, t_ff_1_q, t_ff_2_q, not_5_out);
  not not_5 (not_5_out, t_ff_3_q);
  not not_6 (not_6_out, t_ff_1_q);
  not not_7 (not_7_out, t_ff_2_q);
  and and_4 (DONE, not_6_out, not_7_out, t_ff_3_q);
  and and_5 (and_5_out, t_ff_1_q, not_8_out, t_ff_3_q);
  not not_8 (not_8_out, t_ff_2_q);
  and and_6 (RAM_A[0], IR_IN[0], MAR_IN);
  and and_7 (RAM_A[1], IR_IN[1], MAR_IN);
  and and_8 (RAM_A[2], IR_IN[2], MAR_IN);
  and and_9 (RAM_A[3], IR_IN[3], MAR_IN);
  Demultiplexer #(.enable("false")) demultiplexer_1 (.out0(R0_OUT), .out1(R1_OUT), .in(MBR_IN), .sel(IR_IN[4]));

  assign MAR_OUT = AR_IN;
  assign RAM_W = DONE;
endmodule
